// Logisim project F3.5_library.circ as structural Verilog
module Decoder_2to4 (
  input  IN0,
  input  IN1,
  input  EN,
  output OUT0,
  output OUT1,
  output OUT2,
  output OUT3
);

  wire not_1_out, not_2_out;

  not not_1 (not_1_out, IN0);
  not not_2 (not_2_out, IN1);
  and and_1 (OUT0, not_1_out, EN, not_2_out);
  and and_2 (OUT1, IN0, EN, not_2_out);
  and and_3 (OUT2, not_1_out, EN, IN1);
  and and_4 (OUT3, IN0, EN, IN1);
endmodule

module Decoder_3to8 (
  input  A0,
  input  A1,
  input  A2,
  input  EN,
  output Y0,
  output Y1,
  output Y2,
  output Y3,
  output Y4,
  output Y5,
  output Y6,
  output Y7
);

  wire decoder_2to4_1_out0, decoder_2to4_1_out1, decoder_2to4_1_out2, decoder_2to4_1_out3,
       decoder_2to4_2_out0, decoder_2to4_2_out1, decoder_2to4_2_out2, decoder_2to4_2_out3, not_1_out;

  not not_1 (not_1_out, A2);
  Decoder_2to4 decoder_2to4_1 (
    .IN0(A0), .IN1(A1), .EN(not_1_out), .OUT0(decoder_2to4_1_out0), .OUT1(decoder_2to4_1_out1),
    .OUT2(decoder_2to4_1_out2), .OUT3(decoder_2to4_1_out3));
  Decoder_2to4 decoder_2to4_2 (
    .IN0(A0), .IN1(A1), .EN(A2), .OUT0(decoder_2to4_2_out0), .OUT1(decoder_2to4_2_out1),
    .OUT2(decoder_2to4_2_out2), .OUT3(decoder_2to4_2_out3));
  and and_1 (Y0, decoder_2to4_1_out0, EN);
  and and_2 (Y1, decoder_2to4_1_out1, EN);
  and and_3 (Y2, decoder_2to4_1_out2, EN);
  and and_4 (Y3, decoder_2to4_1_out3, EN);
  and and_5 (Y4, decoder_2to4_2_out0, EN);
  and and_6 (Y5, decoder_2to4_2_out1, EN);
  and and_7 (Y6, decoder_2to4_2_out2, EN);
  and and_8 (Y7, decoder_2to4_2_out3, EN);
endmodule

module Decoder_4to16 (
  input  A0,
  input  A1,
  input  A2,
  input  A3,
  output Y0,
  output Y1,
  output Y2,
  output Y3,
  output Y4,
  output Y5,
  output Y6,
  output Y7,
  output Y8,
  output Y9,
  output Y10,
  output Y11,
  output Y12,
  output Y13,
  output Y14,
  output Y15
);

  wire not_1_out;

  not not_1 (not_1_out, A3);
  Decoder_3to8 decoder_3to8_1 (
    .A0(A0), .A1(A1), .A2(A2), .EN(not_1_out), .Y0(Y0), .Y1(Y1), .Y2(Y2), .Y3(Y3), .Y4(Y4), .Y5(Y5), .Y6(Y6),
    .Y7(Y7));
  Decoder_3to8 decoder_3to8_2 (
    .A0(A0), .A1(A1), .A2(A2), .EN(A3), .Y0(Y8), .Y1(Y9), .Y2(Y10), .Y3(Y11), .Y4(Y12), .Y5(Y13), .Y6(Y14),
    .Y7(Y15));
endmodule
