// Logisim project F3.7_library.circ as structural Verilog: 8 circuits, main circuit SR_Latch
module SR_Latch (
  input  S,
  input  R,
  output NQ,
  output Q
);

  nor nor_1 (NQ, S, Q);
  nor nor_2 (Q, NQ, R);
endmodule

module D_Latch (
  input  D,
  input  WE,
  output Q,
  output NQ
);

  wire and_1_out, and_2_out, not_1_out;

  not not_1 (not_1_out, D);
  and and_1 (and_1_out, not_1_out, WE);
  and and_2 (and_2_out, WE, D);
  SR_Latch sr_latch_1 (.S(and_1_out), .R(and_2_out), .NQ(Q), .Q(NQ));
endmodule

module D_Latch_RST (
  input  RST,
  input  D,
  input  WE,
  output Q,
  output NQ
);

  wire and_1_out, and_2_out, and_3_out, not_1_out, not_2_out, or_1_out;

  not not_1 (not_1_out, RST);
  not not_2 (not_2_out, D);
  and and_1 (and_1_out, not_2_out, WE);
  and and_2 (and_2_out, D, WE);
  or or_1 (or_1_out, RST, and_1_out);
  and and_3 (and_3_out, not_1_out, and_2_out);
  SR_Latch sr_latch_1 (.S(or_1_out), .R(and_3_out), .NQ(Q), .Q(NQ));
endmodule

module D_Latch_return (
  output out_1
);

  wire d_latch_rst_1_q, dipswitch_1_p1;

  // DipSwitch #(.number(1)) dipswitch_1: pin names not known; wires that end beside it: dipswitch_1_p1
  D_Latch_RST d_latch_rst_1 (.RST(dipswitch_1_p1), .D(out_1), .WE(1'b1), .Q(d_latch_rst_1_q));  // open: NQ
  not not_1 (out_1, d_latch_rst_1_q);
endmodule

module D_Flip_Flop (
  input  D,
  input  CLK,
  output Q
);

  wire d_latch_1_q, not_1_out;

  not not_1 (not_1_out, CLK);
  D_Latch d_latch_1 (.D(D), .WE(not_1_out), .Q(d_latch_1_q));  // open: NQ
  D_Latch d_latch_2 (.D(d_latch_1_q), .WE(CLK), .Q(Q));  // open: NQ
endmodule

module D_Flip_Flop_RST (
  input  RST,
  input  D,
  input  CLK,
  output out_4
);

  wire d_latch_rst_1_q, not_1_out;

  not not_1 (not_1_out, CLK);
  D_Latch_RST d_latch_rst_1 (.RST(RST), .D(D), .WE(not_1_out), .Q(d_latch_rst_1_q));  // open: NQ
  D_Latch_RST d_latch_rst_2 (.RST(RST), .D(d_latch_rst_1_q), .WE(CLK), .Q(out_4));  // open: NQ
endmodule

module D_Flip_Flop_return (
  input  RST,
  input  CLK,
  output out_3
);

  wire d_flip_flop_rst_1_out_4;

  D_Flip_Flop_RST d_flip_flop_rst_1 (.CLK(CLK), .RST(RST), .D(out_3), .out_4(d_flip_flop_rst_1_out_4));
  not not_1 (out_3, d_flip_flop_rst_1_out_4);
endmodule

module D_Flip_Flop_N_Edge (
  input  D,
  input  CLK,
  output Q
);

  wire d_latch_1_q, not_1_out;

  D_Latch d_latch_1 (.D(D), .WE(CLK), .Q(d_latch_1_q));  // open: NQ
  not not_1 (not_1_out, CLK);
  D_Latch d_latch_2 (.D(d_latch_1_q), .WE(not_1_out), .Q(Q));  // open: NQ
endmodule
